# Fritzing sketch ESP32-Cam+DHT11 (saved by Fritzing 0.8.7b)
breadboards: 1

parts:
  DHT11 = DHT11 Humitidy and Temperature Sensor (3 pins)
  ESP32_-_Back1 = ESP32 - CAM

nets:
  N1: DHT11.DATA, ESP32_-_Back1.3.3V_/_5V_/_P_OUT
  N2: DHT11.VDD, ESP32_-_Back1.GPIO13
  N3: DHT11.GND, ESP32_-_Back1.GND#16

custom parts:
  DHT11 Humitidy and Temperature Sensor (3 pins): DHT11 Humidity and Temperature Sensor (3 pins) from the design created by John De Cristofaro for Adafruit Industries.
  ESP32 - CAM: The ESP32-CAM has a very competitive small-size camera module that can operate independently as a minimum system with a footprint of only 27*40.5*4.5mm and a deep sleep current of up to 6mA.
